// Logisim project A Combinational Logic Circuit by Using 3-to-8 line decoders and external logic gates.circ as structural Verilog: 1 circuit, main circuit main
module main (
  input  z2,
  input  z1,
  output out_3,
  output B
);

  wire decoder_1_out0, decoder_1_out1, decoder_1_out2, decoder_1_out3, decoder_1_out4, decoder_1_out5,
       decoder_1_out6, decoder_1_out7;
  wire [2:1] undriven;

  or or_1 (z2, decoder_1_out2, decoder_1_out3, decoder_1_out0, decoder_1_out7);
  or or_2 (z1, decoder_1_out1, decoder_1_out5, decoder_1_out4, decoder_1_out6);
  Decoder #(.select(3), .tristate("true")) decoder_1 (
    .out0(decoder_1_out0), .out1(decoder_1_out1), .out2(decoder_1_out2), .out3(decoder_1_out3),
    .out4(decoder_1_out4), .out5(decoder_1_out5), .out6(decoder_1_out6), .out7(decoder_1_out7),
    .sel({undriven, B}));  // open: en
  // Pins of 1 and 3 bits meet at {undriven, B}

  assign out_3 = B;
endmodule
