// Logisim project AND, OR, NAND, and NOR, XOR gates with LED.circ as structural Verilog: 1 circuit, main circuit main
module main (
  input  S1_1,
  input  S1_1_2,
  input  S1_2,
  input  S1_2_2,
  input  S1_1_3,
  input  S1_1_4,
  input  S1_2_3,
  input  S1_2_4,
  input  S1_1_5,
  input  S1_2_5
);

  wire and_1_out, nand_1_out, nor_1_out, or_1_out, xor_1_out;

  and and_1 (and_1_out, S1_1_3, S1_2_3);
  LED led_1 (.in(nand_1_out));
  nand nand_1 (nand_1_out, S1_1, S1_1, S1_2);
  LED led_2 (.in(and_1_out));
  nor nor_1 (nor_1_out, S1_1_5, S1_2_5);
  LED led_3 (.in(nor_1_out));
  or or_1 (or_1_out, S1_1_2, S1_2_2);
  xor xor_1 (xor_1_out, S1_1_4, S1_2_4);
  LED led_4 (.in(or_1_out));
  LED led_5 (.in(xor_1_out));
endmodule
