// Logisim project AND, OR, NAND, and NOR, XOR gates.circ as structural Verilog: 1 circuit, main circuit main
module main (
  input  S1_1,
  input  in_2,
  input  S1_2,
  input  in_4,
  input  in_5,
  input  in_6,
  input  in_7,
  input  in_8,
  input  in_9,
  input  in_10,
  output out_11,
  output out_12,
  output out_13,
  output out_14,
  output out_15
);

  and and_1 (out_13, in_5, in_7);
  nand nand_1 (out_11, S1_1, S1_1, S1_2);
  nor nor_1 (out_15, in_9, in_10);
  or or_1 (out_12, in_2, in_4);
  xor xor_1 (out_14, in_6, in_8);
endmodule
