// Logisim project BCD to 7-Segment Decoders.circ as structural Verilog: 13 circuits, main circuit 7447
module LEDA (
  input  a,
  input  b,
  input  c,
  input  d,
  output x
);

  wire and_1_out, and_2_out, and_3_out, and_4_out, and_5_out, and_6_out, and_7_out, and_8_out, and_9_out,
       and_10_out, not_1_out, not_2_out, not_3_out, not_4_out, not_5_out, not_6_out, not_7_out, not_8_out,
       not_9_out, or_1_out, or_2_out, or_3_out;

  not not_1 (not_1_out, a);
  and and_1 (and_1_out, not_1_out, not_2_out);
  not not_2 (not_2_out, b);
  not not_3 (not_3_out, d);
  not not_4 (not_4_out, a);
  and and_2 (and_2_out, not_4_out, not_5_out);
  not not_5 (not_5_out, b);
  not not_6 (not_6_out, a);
  not not_7 (not_7_out, b);
  not not_8 (not_8_out, c);
  and and_3 (and_3_out, and_1_out, not_3_out);
  and and_4 (and_4_out, and_2_out, c);
  and and_5 (and_5_out, not_6_out, b);
  and and_6 (and_6_out, a, not_7_out);
  not not_9 (not_9_out, c);
  and and_7 (and_7_out, a, not_8_out);
  or or_1 (or_1_out, and_3_out, and_4_out);
  and and_8 (and_8_out, and_5_out, d);
  and and_9 (and_9_out, and_6_out, not_9_out);
  and and_10 (and_10_out, and_7_out, d);
  or or_2 (or_2_out, or_1_out, and_8_out);
  or or_3 (or_3_out, and_9_out, and_10_out);
  or or_4 (x, or_2_out, or_3_out);
endmodule

module LEDB (
  input  a,
  input  b,
  input  c,
  input  d,
  output x
);

  wire and_1_out, and_2_out, and_3_out, and_4_out, and_5_out, not_1_out, not_2_out, not_3_out, not_4_out,
       not_5_out, not_6_out, not_7_out, or_1_out, or_2_out;

  not not_1 (not_1_out, a);
  not not_2 (not_2_out, b);
  not not_3 (not_3_out, b);
  not not_4 (not_4_out, c);
  not not_5 (not_5_out, c);
  not not_6 (not_6_out, d);
  not not_7 (not_7_out, a);
  and and_1 (and_1_out, not_7_out, c);
  and and_2 (and_2_out, not_1_out, not_2_out);
  and and_3 (and_3_out, not_3_out, not_4_out);
  and and_4 (and_4_out, not_5_out, not_6_out);
  and and_5 (and_5_out, and_1_out, d);
  or or_1 (or_1_out, and_2_out, and_3_out);
  or or_2 (or_2_out, and_4_out, and_5_out);
  or or_3 (x, or_1_out, or_2_out);
endmodule

module LEDC (
  input  a,
  input  b,
  input  c,
  input  d,
  output x
);

  wire and_1_out, and_2_out, and_3_out, not_1_out, not_2_out, not_3_out, not_4_out, or_1_out;

  not not_1 (not_1_out, b);
  and and_1 (and_1_out, not_1_out, not_2_out);
  not not_2 (not_2_out, c);
  not not_3 (not_3_out, b);
  and and_2 (and_2_out, not_3_out, d);
  not not_4 (not_4_out, a);
  or or_1 (or_1_out, and_1_out, and_2_out);
  and and_3 (and_3_out, not_4_out, b);
  or or_2 (x, or_1_out, and_3_out);
endmodule

module LEDD (
  input  a,
  input  b,
  input  c,
  input  d,
  output x
);

  wire and_1_out, and_2_out, and_3_out, and_4_out, and_5_out, not_1_out, not_2_out, not_3_out, not_4_out,
       not_5_out, or_1_out, or_2_out;

  not not_1 (not_1_out, b);
  not not_2 (not_2_out, d);
  not not_3 (not_3_out, b);
  not not_4 (not_4_out, d);
  and and_1 (and_1_out, b, not_5_out);
  not not_5 (not_5_out, c);
  and and_2 (and_2_out, not_1_out, not_2_out);
  and and_3 (and_3_out, not_3_out, c);
  and and_4 (and_4_out, c, not_4_out);
  and and_5 (and_5_out, and_1_out, d);
  or or_1 (or_1_out, and_2_out, and_3_out);
  or or_2 (or_2_out, and_4_out, and_5_out);
  or or_3 (x, or_1_out, or_2_out);
endmodule

module LEDE (
  input  a,
  input  b,
  input  c,
  input  d,
  output x
);

  wire and_1_out, and_2_out, not_1_out, not_2_out, not_3_out;

  not not_1 (not_1_out, b);
  and and_1 (and_1_out, not_1_out, not_2_out);
  not not_2 (not_2_out, d);
  and and_2 (and_2_out, c, not_3_out);
  not not_3 (not_3_out, d);
  or or_1 (x, and_1_out, and_2_out);
endmodule

module LEDF (
  input  a,
  input  b,
  input  c,
  input  d,
  output x
);

  wire and_1_out, and_2_out, and_3_out, and_4_out, not_1_out, not_2_out, not_3_out, not_4_out, not_5_out,
       or_1_out, or_2_out;

  not not_1 (not_1_out, c);
  and and_1 (and_1_out, not_1_out, not_2_out);
  not not_2 (not_2_out, d);
  and and_2 (and_2_out, b, not_3_out);
  not not_3 (not_3_out, c);
  and and_3 (and_3_out, b, not_4_out);
  not not_4 (not_4_out, d);
  and and_4 (and_4_out, a, not_5_out);
  not not_5 (not_5_out, c);
  or or_1 (or_1_out, and_1_out, and_2_out);
  or or_2 (or_2_out, and_3_out, and_4_out);
  or or_3 (x, or_1_out, or_2_out);
endmodule

module LEDG (
  input  a,
  input  b,
  input  c,
  input  d,
  output x
);

  wire and_1_out, and_2_out, and_3_out, and_4_out, not_1_out, not_2_out, not_3_out, not_4_out, or_1_out,
       or_2_out;

  not not_1 (not_1_out, b);
  and and_1 (and_1_out, not_1_out, c);
  and and_2 (and_2_out, b, not_2_out);
  not not_2 (not_2_out, c);
  and and_3 (and_3_out, b, not_3_out);
  not not_3 (not_3_out, d);
  and and_4 (and_4_out, a, not_4_out);
  not not_4 (not_4_out, b);
  or or_1 (or_1_out, and_1_out, and_2_out);
  or or_2 (or_2_out, and_3_out, and_4_out);
  or or_3 (x, or_1_out, or_2_out);
endmodule

module _7447 (
  input  in_1,
  input  in_2,
  input  in_3,
  input  in_4
);

  wire leda_1_x, ledb_1_x, ledc_1_x, ledd_1_x, lede_1_x, ledf_1_x, ledg_1_x;

  LEDA leda_1 (.a(in_1), .b(in_2), .c(in_3), .d(in_4), .x(leda_1_x));
  LEDB ledb_1 (.a(in_1), .b(in_2), .c(in_3), .d(in_4), .x(ledb_1_x));
  LEDC ledc_1 (.a(in_1), .b(in_2), .c(in_3), .d(in_4), .x(ledc_1_x));
  LEDD ledd_1 (.a(in_1), .b(in_2), .c(in_3), .d(in_4), .x(ledd_1_x));
  LEDE lede_1 (.a(in_1), .b(in_2), .c(in_3), .d(in_4), .x(lede_1_x));
  LEDF ledf_1 (.a(in_1), .b(in_2), .c(in_3), .d(in_4), .x(ledf_1_x));
  LEDG ledg_1 (.a(in_1), .b(in_2), .c(in_3), .d(in_4), .x(ledg_1_x));
  _7_Segment_Display u_7_segment_display_1 (
    .g(ledg_1_x), .f(ledf_1_x), .a(leda_1_x), .b(ledb_1_x), .e(lede_1_x), .d(ledd_1_x), .c(ledc_1_x));  // open: dp
endmodule

// 93
module _7493 (
  input  VCC,
  input  CLOCK_0,
  input  CLOCK_1,
  input  CLEAR_0,
  input  CLEAR_1,
  input  GND,
  output Q1,
  output Q2,
  output Q3,
  output Q4
);

  wire and_1_out, d_flip_flop_1_r, d_flip_flop_2_r, d_flip_flop_3_r, d_flip_flop_4_r, not_1_out, not_2_out,
       not_3_out, not_4_out;

  not not_1 (not_1_out, CLOCK_0);
  not not_2 (not_2_out, CLOCK_1);
  and and_1 (and_1_out, CLEAR_0, CLEAR_1);
  not not_3 (not_3_out, Q2);
  not not_4 (not_4_out, Q3);
  D_Flip_Flop d_flip_flop_1 (
    .D(d_flip_flop_1_r), .Clock(not_1_out), .Clear(and_1_out), .Q(Q1), .R(d_flip_flop_1_r));  // open: Set
  D_Flip_Flop d_flip_flop_2 (.D(d_flip_flop_2_r), .Clock(not_2_out), .Q(Q2), .R(d_flip_flop_2_r));  // open: Set, Clear
  D_Flip_Flop d_flip_flop_3 (
    .D(d_flip_flop_3_r), .Clock(not_3_out), .Clear(and_1_out), .Q(Q3), .R(d_flip_flop_3_r));  // open: Set
  D_Flip_Flop d_flip_flop_4 (
    .D(d_flip_flop_4_r), .Clock(not_4_out), .Clear(and_1_out), .Q(Q4), .R(d_flip_flop_4_r));  // open: Set
endmodule

// D-FF
module D_Flip_Flop (
  input  Set,
  input  D,
  input  Clock,
  input  Clear,
  output Q,
  output R
);

  D_Flip_Flop_part d_ff_1 (.clk(Clock), .D(D), .Q(Q), .Qn(R), .preset(Set), .reset(Clear));  // open: en
endmodule

// 47
module _7447_Decoder (
  input  I4,
  input  I3,
  input  I2,
  input  I1,
  output o1,
  output o2,
  output o3,
  output o5,
  output o6,
  output o7,
  output o8
);

  wire and_1_out, and_2_out, and_3_out, and_4_out, and_5_out, and_6_out, and_7_out, and_8_out, and_9_out,
       and_10_out, and_11_out, and_12_out, and_13_out, and_14_out, and_15_out, and_16_out, and_17_out,
       and_18_out, and_19_out, and_20_out, and_21_out, and_22_out, and_23_out, and_24_out, and_25_out,
       and_26_out, and_27_out, and_28_out, and_29_out, and_30_out, and_31_out, and_32_out, and_33_out,
       and_34_out, and_35_out, and_36_out, not_1_out, not_2_out, not_3_out, not_4_out, not_5_out, not_6_out,
       not_7_out, not_8_out, not_9_out, not_10_out, not_11_out, not_12_out, not_13_out, not_14_out,
       not_15_out, not_16_out, not_17_out, not_18_out, not_19_out, not_20_out, not_21_out, not_22_out,
       not_23_out, not_24_out, not_25_out, not_26_out, not_27_out, not_28_out, not_29_out, not_30_out,
       not_31_out, not_32_out, not_33_out, not_34_out, not_35_out, not_36_out, not_37_out, not_38_out,
       not_39_out, not_40_out, not_41_out, not_42_out, not_43_out, not_44_out, not_45_out;

  not not_1 (not_1_out, I3);
  and and_1 (and_1_out, not_1_out, not_2_out);
  not not_2 (not_2_out, I1);
  and and_2 (and_2_out, I2, not_3_out);
  not not_3 (not_3_out, I1);
  and and_3 (and_3_out, I4, I2);
  and and_4 (and_4_out, I4, I3);
  not not_4 (not_4_out, I3);
  and and_5 (and_5_out, not_4_out, not_5_out, not_6_out);
  not not_5 (not_5_out, I2);
  not not_6 (not_6_out, I1);
  not not_7 (not_7_out, I4);
  and and_6 (and_6_out, not_7_out, I2, not_8_out);
  not not_8 (not_8_out, I1);
  not not_9 (not_9_out, I3);
  and and_7 (and_7_out, not_9_out, I2, I1);
  not not_10 (not_10_out, I2);
  and and_8 (and_8_out, I3, not_10_out, I1);
  and and_9 (and_9_out, I4, I3, not_11_out);
  not not_11 (not_11_out, I1);
  not not_12 (not_12_out, I3);
  and and_10 (and_10_out, not_12_out, not_13_out);
  not not_13 (not_13_out, I2);
  not not_14 (not_14_out, I3);
  and and_11 (and_11_out, not_14_out, I1);
  not not_15 (not_15_out, I2);
  and and_12 (and_12_out, not_15_out, I1);
  not not_16 (not_16_out, I4);
  and and_13 (and_13_out, not_16_out, I3);
  and and_14 (and_14_out, I4, not_17_out);
  not not_17 (not_17_out, I3);
  not not_18 (not_18_out, I3);
  and and_15 (and_15_out, not_18_out, I2);
  and and_16 (and_16_out, I2, not_19_out);
  not not_19 (not_19_out, I1);
  not not_20 (not_20_out, I4);
  and and_17 (and_17_out, not_20_out, I3, not_21_out);
  not not_21 (not_21_out, I1);
  and and_18 (and_18_out, I3, not_22_out, I1);
  not not_22 (not_22_out, I2);
  and and_19 (and_19_out, I4, not_23_out);
  not not_23 (not_23_out, I3);
  and and_20 (and_20_out, I4, I2);
  not not_24 (not_24_out, I2);
  and and_21 (and_21_out, not_24_out, not_25_out);
  not not_25 (not_25_out, I1);
  not not_26 (not_26_out, I4);
  and and_22 (and_22_out, not_26_out, I3, not_27_out);
  not not_27 (not_27_out, I2);
  and and_23 (and_23_out, I3, not_28_out);
  not not_28 (not_28_out, I1);
  and and_24 (and_24_out, I4, not_29_out);
  not not_29 (not_29_out, I3);
  and and_25 (and_25_out, I4, I2);
  not not_30 (not_30_out, I3);
  and and_26 (and_26_out, not_30_out, not_31_out);
  not not_31 (not_31_out, I1);
  not not_32 (not_32_out, I4);
  and and_27 (and_27_out, not_32_out, I2, I1);
  not not_33 (not_33_out, I4);
  and and_28 (and_28_out, not_33_out, I3, I1);
  and and_29 (and_29_out, I3, I2, I1);
  and and_30 (and_30_out, I4, not_34_out, not_35_out);
  not not_34 (not_34_out, I3);
  not not_35 (not_35_out, I2);
  and and_31 (and_31_out, I4, not_36_out);
  not not_36 (not_36_out, I1);
  not not_37 (not_37_out, I4);
  and and_32 (and_32_out, not_37_out, not_38_out, not_39_out);
  not not_38 (not_38_out, I2);
  not not_39 (not_39_out, I1);
  not not_40 (not_40_out, I3);
  and and_33 (and_33_out, not_40_out, not_41_out);
  not not_41 (not_41_out, I2);
  not not_42 (not_42_out, I3);
  and and_34 (and_34_out, not_42_out, not_43_out);
  not not_43 (not_43_out, I1);
  not not_44 (not_44_out, I4);
  and and_35 (and_35_out, not_44_out, I2, I1);
  not not_45 (not_45_out, I2);
  and and_36 (and_36_out, I4, not_45_out, I1);
  or or_1 (o1, and_1_out, and_2_out, and_3_out, and_4_out);
  or or_2 (o2, and_5_out, and_6_out, and_7_out, and_8_out, and_9_out);
  or or_3 (o3, and_10_out, and_11_out, and_12_out, and_13_out, and_14_out);
  or or_4 (o6, and_21_out, and_22_out, and_23_out, and_24_out, and_25_out);
  or or_5 (o8, and_32_out, and_33_out, and_34_out, and_35_out, and_36_out);
  or or_6 (o5, and_15_out, and_16_out, and_17_out, and_18_out, and_19_out, and_20_out);
  or or_7 (o7, and_26_out, and_27_out, and_28_out, and_29_out, and_30_out, and_31_out);
endmodule

module _4_Bit_counter (
  input  T,
  input  Reset,
  output Q3,
  output Q2,
  output Q1,
  output Q0
);

  wire t_ff_1_qn, t_ff_2_qn, t_ff_3_qn;

  T_Flip_Flop t_ff_1 (.clk(T), .T(1'b1), .Q(Q0), .Qn(t_ff_1_qn), .reset(Reset));  // open: preset, en
  T_Flip_Flop t_ff_2 (.clk(t_ff_1_qn), .T(1'b1), .Q(Q1), .Qn(t_ff_2_qn), .reset(Reset));  // open: preset, en
  T_Flip_Flop t_ff_3 (.clk(t_ff_2_qn), .T(1'b1), .Q(Q2), .Qn(t_ff_3_qn), .reset(Reset));  // open: preset, en
  T_Flip_Flop t_ff_4 (.clk(t_ff_3_qn), .T(1'b1), .Q(Q3), .reset(Reset));  // open: Qn, preset, en
endmodule

module Binary_Counter_Circuit (
  input  VCC
);

  wire CLOCK_out, n7447_decoder_1_o1, n7447_decoder_1_o2, n7447_decoder_1_o3, n7447_decoder_1_o5,
       n7447_decoder_1_o6, n7447_decoder_1_o7, n7447_decoder_1_o8, n7493_1_q1, n7493_1_q2, n7493_1_q3,
       n7493_1_q4;

  Clock CLOCK (.out(CLOCK_out));
  _7493 u_7493_1 (
    .VCC(VCC), .CLOCK_0(CLOCK_out), .CLOCK_1(n7493_1_q1), .CLEAR_0(n7493_1_q4), .CLEAR_1(n7493_1_q4),
    .GND(1'b0), .Q1(n7493_1_q1), .Q2(n7493_1_q2), .Q3(n7493_1_q3), .Q4(n7493_1_q4));
  _7447_Decoder u_7447_decoder_1 (
    .I4(n7493_1_q1), .I3(n7493_1_q2), .I2(n7493_1_q3), .I1(n7493_1_q4), .o1(n7447_decoder_1_o1),
    .o2(n7447_decoder_1_o2), .o3(n7447_decoder_1_o3), .o5(n7447_decoder_1_o5), .o6(n7447_decoder_1_o6),
    .o7(n7447_decoder_1_o7), .o8(n7447_decoder_1_o8));
  _7_Segment_Display u_7_segment_display_1 (
    .g(n7447_decoder_1_o5), .f(n7447_decoder_1_o6), .a(n7447_decoder_1_o7), .b(n7447_decoder_1_o8),
    .e(n7447_decoder_1_o1), .d(n7447_decoder_1_o2), .c(n7447_decoder_1_o3));  // open: dp
endmodule
