// Logisim project Binary Counter Circuit No. 1.circ as structural Verilog: 3 circuits, main circuit main
module main (
  input  VCC,
  output QA,
  output QB,
  output QC,
  output QD
);

  wire CLOCK_out;

  Clock CLOCK (.out(CLOCK_out));
  _7493 u_7493_1 (
    .VCC(VCC), .CLOCK_0(CLOCK_out), .CLOCK_1(QA), .CLEAR_0(1'b0), .CLEAR_1(1'b0), .GND(1'b0), .Q1(QA),
    .Q2(QB), .Q3(QC), .Q4(QD));
endmodule

module _7493 (
  input  VCC,
  input  CLOCK_0,
  input  CLOCK_1,
  input  CLEAR_0,
  input  CLEAR_1,
  input  GND,
  output Q1,
  output Q2,
  output Q3,
  output Q4
);

  wire and_1_out, d_flip_flop_1_r, d_flip_flop_2_r, d_flip_flop_3_r, d_flip_flop_4_r, not_1_out, not_2_out,
       not_3_out, not_4_out;

  not not_1 (not_1_out, CLOCK_0);
  not not_2 (not_2_out, CLOCK_1);
  and and_1 (and_1_out, CLEAR_0, CLEAR_1);
  not not_3 (not_3_out, Q2);
  not not_4 (not_4_out, Q3);
  D_flip_flop d_flip_flop_1 (
    .D(d_flip_flop_1_r), .Clock(not_1_out), .Clear(and_1_out), .Q(Q1), .R(d_flip_flop_1_r));  // open: Set
  D_flip_flop d_flip_flop_2 (
    .D(d_flip_flop_2_r), .Clock(not_2_out), .Clear(and_1_out), .Q(Q2), .R(d_flip_flop_2_r));  // open: Set
  D_flip_flop d_flip_flop_3 (
    .D(d_flip_flop_3_r), .Clock(not_3_out), .Clear(and_1_out), .Q(Q3), .R(d_flip_flop_3_r));  // open: Set
  D_flip_flop d_flip_flop_4 (
    .D(d_flip_flop_4_r), .Clock(not_4_out), .Clear(and_1_out), .Q(Q4), .R(d_flip_flop_4_r));  // open: Set
endmodule

// D-FF
module D_flip_flop (
  input  Set,
  input  D,
  input  Clock,
  input  Clear,
  output Q,
  output R
);

  D_Flip_Flop d_ff_1 (.clk(Clock), .D(D), .Q(Q), .Qn(R), .preset(Set), .reset(Clear));  // open: en
endmodule
