// Logisim project Boolean expressions 1.circ as structural Verilog: 1 circuit, main circuit main
module main (
  input  X1,
  input  X1_2,
  input  X2,
  input  X1_3,
  input  X1_4,
  input  X2_2,
  input  X2_3,
  input  X3,
  input  X1_5,
  input  X2_4,
  output Y,
  output Y_2,
  output Y_3,
  output out_14,
  output Y1,
  output Y2
);

  wire nand_1_out, nand_2_out, nand_3_out, nor_1_out, xor_1_out;

  nand nand_1 (nand_1_out, X1, X1);
  nand nand_2 (nand_2_out, X2, X2);
  nand nand_3 (nand_3_out, X1_3, X2_2);
  nand nand_4 (Y, nand_1_out, nand_2_out);
  nand nand_5 (Y_3, nand_3_out, nand_3_out);
  nor nor_1 (nor_1_out, X1_5, X2_4);
  and and_1 (Y2, X1_5, X2_4);
  nor nor_2 (Y1, nor_1_out, Y2);
  nand nand_6 (Y_2, X1_2, X1_2);
  xor xor_1 (xor_1_out, X1_4, X2_3);
  xor xor_2 (out_14, xor_1_out, X3);
endmodule
