// Logisim project Boolean expressions 2.circ as structural Verilog: 1 circuit, main circuit main
module main (
  input  S1_1
);

  wire not_1_out;

  not not_1 (not_1_out, S1_1);
  LED LED_1 (.in(not_1_out));
endmodule
