// Logisim project Circuit by using D flip flops and external gates.circ as structural Verilog: 1 circuit, main circuit main
module main (
  input  X,
  output W,
  output Y,
  output Z
);

  wire A_q, A_qn, and_1_out, and_2_out, and_3_out, and_4_out, B_q, clock_1_out, not_1_out, xor_1_out;

  not not_1 (not_1_out, X);
  and and_1 (and_1_out, A_q, not_1_out);
  and and_2 (and_2_out, X, B_q);
  and and_3 (and_3_out, A_qn, X);
  and and_4 (and_4_out, B_q, not_1_out);
  Clock clock_1 (.out(clock_1_out));
  or or_1 (W, and_1_out, and_2_out);
  or or_2 (Y, and_3_out, and_4_out);
  D_Flip_Flop A (.clk(clock_1_out), .D(W), .Q(A_q), .Qn(A_qn));  // open: preset, en, reset
  D_Flip_Flop B (.clk(clock_1_out), .D(Y), .Q(B_q));  // open: Qn, preset, en, reset
  xor xor_1 (xor_1_out, A_q, B_q);
  not not_2 (Z, xor_1_out);

  // Notes on the sheet:
  //   Input
  //   Present state
  //   Next state
  //   Output
endmodule
