// Logisim project Circuit drawing with LED control using 7474 circuit.circ as structural Verilog: 1 circuit, main circuit main
module main (
  input  B,
  input  X,
  input  A,
  output W,
  output Y,
  output Z
);

  wire and_1_out, and_2_out, and_3_out, and_4_out, clock_1_out, n7474_1_p5, n7474_1_p6, n7474_1_p10,
       n7474_1_p11, not_1_out, not_2_out, not_3_out, xor_1_out;

  not not_1 (not_1_out, X);
  and and_1 (and_1_out, n7474_1_p5, not_1_out);
  and and_2 (and_2_out, X, n7474_1_p11);
  and and_3 (and_3_out, n7474_1_p6, X);
  and and_4 (and_4_out, n7474_1_p11, not_1_out);
  or or_1 (W, and_1_out, and_2_out);
  not not_2 (not_2_out, A);
  or or_2 (Y, and_3_out, and_4_out);
  not not_3 (not_3_out, not_2_out);
  Clock clock_1 (.out(clock_1_out));
  // _7474 7474_1: pin names not known; wires that end beside it: not_3_out, W, clock_1_out, not_2_out, n7474_1_p5, n7474_1_p6, 1'b0, Y, clock_1_out, n7474_1_p10, n7474_1_p11
  not not_4 (n7474_1_p10, B);
  xor xor_1 (xor_1_out, n7474_1_p11, n7474_1_p5);
  LED u_A (.in(n7474_1_p5));
  LED u_B (.in(n7474_1_p11));
  not not_5 (Z, xor_1_out);

  // Notes on the sheet:
  //   Input
  //   Present state
  //   Next state
  //   Output
endmodule
