// Logisim project Combinational Logic Circuit by Using One 74154 Decoder and only NAND Gates.circ as structural Verilog: 2 circuits, main circuit main
module main (
  input  A,
  input  B,
  input  B_2,
  input  B_3,
  output z1,
  output z2
);

  _74154 u_74154_1 (
    .A(A), .B(B), .C(B_2), .D(B_3), ._5(z1), ._9(z2));  // open: G1, G2, _0, _1, _2, _3, _4, _6, _7, _8, _10, _11, _12, _13, _14, _15
endmodule

module _74154 (
  input  G1,
  input  G2,
  input  A,
  input  B,
  input  C,
  input  D,
  output _0,
  output _1,
  output _2,
  output _3,
  output _4,
  output _5,
  output _6,
  output _7,
  output _8,
  output _9,
  output _10,
  output _11,
  output _12,
  output _13,
  output _14,
  output _15
);

  wire nand_1_out, not_1_out, not_2_out, not_3_out, not_4_out, not_5_out, not_6_out, not_7_out, not_8_out;

  not not_1 (not_1_out, A);
  not not_2 (not_2_out, B);
  not not_3 (not_3_out, C);
  not not_4 (not_4_out, D);
  nand nand_1 (nand_1_out, G1, G2);
  not not_5 (not_5_out, not_1_out);
  not not_6 (not_6_out, not_2_out);
  not not_7 (not_7_out, not_3_out);
  not not_8 (not_8_out, not_4_out);
  nand nand_2 (_0, nand_1_out, not_1_out, not_2_out, not_3_out, not_4_out);
  nand nand_3 (_1, nand_1_out, not_5_out, not_2_out, not_3_out, not_4_out);
  nand nand_4 (_2, nand_1_out, not_1_out, not_6_out, not_3_out, not_4_out);
  nand nand_5 (_3, nand_1_out, not_5_out, not_6_out, not_3_out, not_4_out);
  nand nand_6 (_4, nand_1_out, not_1_out, not_2_out, not_7_out, not_4_out);
  nand nand_7 (_5, nand_1_out, not_5_out, not_2_out, not_7_out, not_4_out);
  nand nand_8 (_6, nand_1_out, not_1_out, not_6_out, not_7_out, not_4_out);
  nand nand_9 (_7, nand_1_out, not_5_out, not_6_out, not_7_out, not_4_out);
  nand nand_10 (_8, nand_1_out, not_1_out, not_2_out, not_3_out, not_8_out);
  nand nand_11 (_9, nand_1_out, not_5_out, not_2_out, not_3_out, not_8_out);
  nand nand_12 (_10, nand_1_out, not_1_out, not_6_out, not_3_out, not_8_out);
  nand nand_13 (_11, nand_1_out, not_5_out, not_6_out, not_3_out, not_8_out);
  nand nand_14 (_12, nand_1_out, not_1_out, not_2_out, not_7_out, not_8_out);
  nand nand_15 (_13, nand_1_out, not_5_out, not_2_out, not_7_out, not_8_out);
  nand nand_16 (_14, nand_1_out, not_1_out, not_6_out, not_7_out, not_8_out);
  nand nand_17 (_15, nand_1_out, not_5_out, not_6_out, not_7_out, not_8_out);
endmodule
