// Logisim project D Flip-Flop Circuit.circ as structural Verilog: 3 circuits, main circuit main
module main (
  input  Clear,
  input  D,
  input  Clock,
  input  Preset,
  output Q,
  output Q_prime
);

  _7474 u_7474_1 (
    .Clr1(Clear), .D1(D), .Clk1(Clock), .Preset1(Preset), .Q1(Q), .Q1_prime(Q_prime));  // open: Clr2, D2, Clk2, Preset2, Q2, Q2_prime
endmodule

module _7474 (
  input  Clr2,
  input  Clr1,
  input  D2,
  input  D1,
  input  Clk2,
  input  Clk1,
  input  Preset2,
  input  Preset1,
  output Q2,
  output Q1,
  output Q2_prime,
  output Q1_prime
);

  D_Flip_Flop d_flip_flop_1 (.Preset(Preset1), .D(D1), .Clk(Clk1), .Clr(Clr1), .Q(Q1), .Q_prime(Q1_prime));
  D_Flip_Flop d_flip_flop_2 (.Preset(Preset2), .D(D2), .Clk(Clk2), .Clr(Clr2), .Q(Q2), .Q_prime(Q2_prime));
endmodule

module D_Flip_Flop (
  input  Preset,
  input  D,
  input  Clk,
  input  Clr,
  output Q,
  output Q_prime
);

  wire nand_1_out, nand_2_out, nand_3_out, nand_4_out, nand_5_out, nand_6_out, not_1_out, not_2_out;

  not not_1 (not_1_out, D);
  nand nand_1 (nand_1_out, D, Clk);
  nand nand_2 (nand_2_out, Clk, not_1_out);
  not not_2 (not_2_out, Clk);
  nand nand_3 (nand_3_out, Preset, nand_1_out, nand_4_out);
  nand nand_4 (nand_4_out, nand_3_out, nand_2_out, Clr);
  nand nand_5 (nand_5_out, nand_3_out, not_2_out);
  nand nand_6 (nand_6_out, not_2_out, nand_4_out);
  nand nand_7 (Q, Preset, nand_5_out, Q_prime);
  nand nand_8 (Q_prime, Q, nand_6_out, Clr);
endmodule
