// Logisim project Full Adder.circ as structural Verilog: 1 circuit, main circuit main
module main (
  input  A,
  input  B,
  input  CARRY_in,
  output SUM,
  output CARRY_out
);

  wire nand_1_out, nand_2_out, xor_1_out;

  xor xor_1 (xor_1_out, A, B);
  nand nand_1 (nand_1_out, A, B);
  xor xor_2 (SUM, xor_1_out, CARRY_in);
  nand nand_2 (nand_2_out, CARRY_in, xor_1_out);
  nand nand_3 (CARRY_out, nand_2_out, nand_1_out);
endmodule
