// Logisim project Half Adder.circ as structural Verilog: 1 circuit, main circuit main
module main (
  input  A,
  input  B,
  output SUM,
  output CARRY
);

  wire nand_1_out;

  xor xor_1 (SUM, A, B);
  nand nand_1 (nand_1_out, A, B);
  not not_1 (CARRY, nand_1_out);
endmodule
