// Logisim project Parity generator by using a 74151 Multiplexer.circ as structural Verilog: 2 circuits, main circuit main
module main (
  input  D,
  input  A,
  input  B,
  input  C,
  input  in_5,
  output out_6
);

  wire not_1_out, not_2_out;

  not not_1 (not_1_out, D);
  not not_2 (not_2_out, in_5);
  _74151 u_74151_1 (
    .A(D), .B(not_1_out), .C(not_1_out), .D(D), .E(not_1_out), .F(D), .G(D), .J(not_1_out), .S0(A), .S1(B),
    .S2(C), .S3(not_2_out), .Y(out_6));  // open: Z
endmodule

module _74151 (
  input  A,
  input  B,
  input  C,
  input  D,
  input  E,
  input  F,
  input  G,
  input  J,
  input  S0,
  input  S1,
  input  S2,
  input  S3,
  output Y,
  output Z
);

  wire and_1_out, and_2_out, and_3_out, and_4_out, and_5_out, and_6_out, and_7_out, and_8_out, not_1_out,
       not_2_out, not_3_out, not_4_out;

  not not_1 (not_1_out, S0);
  not not_2 (not_2_out, S1);
  not not_3 (not_3_out, S3);
  not not_4 (not_4_out, S2);
  and and_1 (and_1_out, A, not_3_out, not_1_out, not_2_out, not_4_out);
  and and_2 (and_2_out, B, not_3_out, S0, not_2_out, not_4_out);
  and and_3 (and_3_out, C, not_3_out, not_1_out, S1, not_4_out);
  and and_4 (and_4_out, D, not_3_out, S0, S1, not_4_out);
  and and_5 (and_5_out, E, not_3_out, not_1_out, not_2_out, S2);
  and and_6 (and_6_out, F, not_3_out, S0, not_2_out, S2);
  and and_7 (and_7_out, G, not_3_out, not_1_out, S1, S2);
  and and_8 (and_8_out, J, not_3_out, S0, S1, S2);
  or or_1 (Y, and_1_out, and_2_out, and_3_out, and_4_out, and_5_out, and_6_out, and_7_out, and_8_out);
  not not_5 (Z, Y);
endmodule
