// Logisim project Response of Logic Gates 1.circ as structural Verilog: 1 circuit, main circuit main
module main (
  input  A,
  input  B,
  output E
);

  wire nand_1_out, nor_1_out;

  nor nor_1 (nor_1_out, A, B);
  nand nand_1 (nand_1_out, A, B);
  xor xor_1 (E, nor_1_out, nand_1_out);
endmodule
