// Logisim project Response of Logic Gates 2.circ as structural Verilog: 1 circuit, main circuit main
module main (
  input  A,
  input  B,
  output D
);

  wire nand_1_out;

  nand nand_1 (nand_1_out, B, B);
  nand nand_2 (D, A, nand_1_out);
endmodule
